# Fritzing sketch ITDS282_Sec2_Group14_Fritzing (saved by Fritzing 1.0.4)
breadboards: 1

parts:
  LED1 = LED - 3mm [color="Red (633nm)" current=0.030A package="3 mm [THT]"]
  M1 = DOIT Esp32 DevKit v1 (30 pins long, 11 pins width) [part_number=ESP32S-PIN30]
  ZS-042_RTC1 = ZS-042 RTC Module
  DHT1 = DHT22 Humidity and Temperature Sensor
  S1 = Pushbutton [package="[THT]"]

nets:
  GND: LED1.cathode, LED1.anode, M1.GND, M1.D23, ZS-042_RTC1.GND, S1.Pin_3, S1.Pin_4
  N1: M1.D21, ZS-042_RTC1.SDA
  N2: M1.D22, ZS-042_RTC1.SCL
  N3: M1.D34, DHT1.VDD
  N4: M1.D35, DHT1.DATA
  N5: M1.D32, DHT1.NULL
  N6: M1.D13, ZS-042_RTC1.VCC
  N7: S1.Pin_1, S1.Pin_2

custom parts:
  DOIT Esp32 DevKit v1 (30 pins long, 11 pins width): The DOIT Esp32 DevKit v1 is one of the development board created by DOIT to evaluate the ESP-WROOM-32 module. It is based on the ESP32 microcontroller that boasts Wifi, Bluetooth, Ethernet and Low Power support all in a single chip. (vanepp) made breadboard work, adjusted pin numbering and labels and reduced size of schematic and cleaned up pcb. This chip is 30pins long (2 x15) and 11 pins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
